// Digital circuit Incrementer (1 bit).dig as structural Verilog
module Incrementer__1_bit (
  input  A,
  input  B,
  input  C,
  output S,
  output V
);

  wire half_adder_1_s, half_adder_1_v, half_adder_2_v;

  Half_Adder half_adder_1 (.A(A), .B(B), .S(half_adder_1_s), .V(half_adder_1_v));
  Half_Adder half_adder_2 (.A(half_adder_1_s), .B(C), .S(S), .V(half_adder_2_v));
  or or_1 (V, half_adder_1_v, half_adder_2_v);
endmodule
