// Digital circuit Half Subtractor.dig as structural Verilog
module Half_Subtractor (
  input  A,
  input  B,
  output S,
  output V
);

  xor xor_1 (S, A, B);
  and and_1 (V, B, ~A);  // And
endmodule
