// Digital circuit Subtractor (16 bit).dig as structural Verilog
module Subtractor__16_bit (
  input  [15:0] A,
  input  [15:0] B,
  input  C,
  output [15:0] S,
  output V
);

  wire subtractor__8_bit_1_v;

  Subtractor__8_bit subtractor__8_bit_1 (.A(A[7:0]), .B(B[7:0]), .C(C), .S(S[7:0]), .V(subtractor__8_bit_1_v));
  Subtractor__8_bit subtractor__8_bit_2 (.A(A[15:8]), .B(B[15:8]), .C(subtractor__8_bit_1_v), .S(S[15:8]), .V(V));
endmodule
