// Digital circuit Subtractor (2 bit).dig as structural Verilog
module Subtractor__2_bit (
  input  [1:0] A,
  input  [1:0] B,
  input  C,
  output [1:0] S,
  output V
);

  wire subtractor__1_bit_1_v;

  Subtractor__1_bit subtractor__1_bit_1 (.A(A[0]), .B(B[0]), .C(C), .S(S[0]), .V(subtractor__1_bit_1_v));
  Subtractor__1_bit subtractor__1_bit_2 (.A(A[1]), .B(B[1]), .C(subtractor__1_bit_1_v), .S(S[1]), .V(V));
endmodule
