// Digital circuit Subtractor (4 bit).dig as structural Verilog
module Subtractor__4_bit (
  input  [3:0] A,
  input  [3:0] B,
  input  C,
  output [3:0] S,
  output V
);

  wire subtractor__2_bit_1_v;

  Subtractor__2_bit subtractor__2_bit_1 (.A(A[1:0]), .B(B[1:0]), .C(C), .S(S[1:0]), .V(subtractor__2_bit_1_v));
  Subtractor__2_bit subtractor__2_bit_2 (.A(A[3:2]), .B(B[3:2]), .C(subtractor__2_bit_1_v), .S(S[3:2]), .V(V));
endmodule
