// Digital circuit Multiplexer (32x1 bit).dig as structural Verilog
module Multiplexer__32x1_bit (
  input  [31:0] sig,
  input  [4:0] sel,
  output Z
);

  wire and_1_out, and_2_out, multiplexer__16x1_bit_1_z, multiplexer__16x1_bit_2_z;

  Multiplexer__16x1_bit multiplexer__16x1_bit_1 (.sig(sig[15:0]), .sel(sel[3:0]), .Z(multiplexer__16x1_bit_1_z));
  Multiplexer__16x1_bit multiplexer__16x1_bit_2 (.sig(sig[31:16]), .sel(sel[3:0]), .Z(multiplexer__16x1_bit_2_z));
  and and_1 (and_1_out, multiplexer__16x1_bit_1_z, ~sel[4]);  // And
  and and_2 (and_2_out, multiplexer__16x1_bit_2_z, sel[4]);
  or or_1 (Z, and_1_out, and_2_out);
endmodule
