// Digital circuit Multiplexer (4x1 bit).dig as structural Verilog
module Multiplexer__4x1_bit (
  input  [3:0] sig,
  input  [1:0] sel,
  output Z
);

  wire and_1_out, and_2_out, multiplexer__2x1_bit_1_z, multiplexer__2x1_bit_2_z;

  Multiplexer__2x1_bit multiplexer__2x1_bit_1 (.sig(sig[1:0]), .sel(sel[0]), .Z(multiplexer__2x1_bit_1_z));
  Multiplexer__2x1_bit multiplexer__2x1_bit_2 (.sig(sig[3:2]), .sel(sel[0]), .Z(multiplexer__2x1_bit_2_z));
  and and_1 (and_1_out, multiplexer__2x1_bit_1_z, ~sel[1]);  // And
  and and_2 (and_2_out, multiplexer__2x1_bit_2_z, sel[1]);
  or or_1 (Z, and_1_out, and_2_out);
endmodule
