// Digital circuit Multiplexer (8x1 bit).dig as structural Verilog
module Multiplexer__8x1_bit (
  input  [7:0] sig,
  input  [2:0] sel,
  output Z
);

  wire and_1_out, and_2_out, multiplexer__4x1_bit_1_z, multiplexer__4x1_bit_2_z;

  Multiplexer__4x1_bit multiplexer__4x1_bit_1 (.sig(sig[3:0]), .sel(sel[1:0]), .Z(multiplexer__4x1_bit_1_z));
  Multiplexer__4x1_bit multiplexer__4x1_bit_2 (.sig(sig[7:4]), .sel(sel[1:0]), .Z(multiplexer__4x1_bit_2_z));
  and and_1 (and_1_out, multiplexer__4x1_bit_1_z, ~sel[2]);  // And
  and and_2 (and_2_out, multiplexer__4x1_bit_2_z, sel[2]);
  or or_1 (Z, and_1_out, and_2_out);
endmodule
