// Digital circuit Voting (3 bit).dig as structural Verilog
module Voting__3_bit (
  input  A,
  input  B,
  input  C,
  output Q
);

  wire and_1_out, and_2_out, and_3_out;

  and and_1 (and_1_out, A, B);
  and and_2 (and_2_out, A, C);
  and and_3 (and_3_out, B, C);
  or or_1 (Q, and_1_out, and_2_out, and_3_out);
endmodule
