// Digital circuit Adder (2 bit).dig as structural Verilog
module Adder__2_bit (
  input  [1:0] A,
  input  [1:0] B,
  input  C,
  output [1:0] S,
  output V
);

  wire adder__1_bit_1_v;

  Adder__1_bit adder__1_bit_1 (.A(A[0]), .B(B[0]), .C(C), .S(S[0]), .V(adder__1_bit_1_v));
  Adder__1_bit adder__1_bit_2 (.A(A[1]), .B(B[1]), .C(adder__1_bit_1_v), .S(S[1]), .V(V));
endmodule
