// Digital circuit Adder (32 bit).dig as structural Verilog
module Adder__32_bit (
  input  [31:0] A,
  input  [31:0] B,
  input  C,
  output [31:0] S,
  output V
);

  wire adder__16_bit_1_v;

  Adder__16_bit adder__16_bit_1 (.A(A[15:0]), .B(B[15:0]), .C(C), .S(S[15:0]), .V(adder__16_bit_1_v));
  Adder__16_bit adder__16_bit_2 (.A(A[31:16]), .B(B[31:16]), .C(adder__16_bit_1_v), .S(S[31:16]), .V(V));
endmodule
