// Digital circuit Adder (8 bit).dig as structural Verilog
module Adder__8_bit (
  input  [7:0] A,
  input  [7:0] B,
  input  C,
  output [7:0] S,
  output V
);

  wire adder__4_bit_1_v;

  Adder__4_bit adder__4_bit_1 (.A(A[3:0]), .B(B[3:0]), .S_2(C), .S(S[3:0]), .V(adder__4_bit_1_v));
  Adder__4_bit adder__4_bit_2 (.A(A[7:4]), .B(B[7:4]), .S_2(adder__4_bit_1_v), .S(S[7:4]), .V(V));
endmodule
