// Digital circuit Subtractor (8 bit).dig as structural Verilog
module Subtractor__8_bit (
  input  [7:0] A,
  input  [7:0] B,
  input  C,
  output [7:0] S,
  output V
);

  wire subtractor__4_bit_1_v;

  Subtractor__4_bit subtractor__4_bit_1 (.A(A[3:0]), .B(B[3:0]), .C(C), .S(S[3:0]), .V(subtractor__4_bit_1_v));
  Subtractor__4_bit subtractor__4_bit_2 (.A(A[7:4]), .B(B[7:4]), .C(subtractor__4_bit_1_v), .S(S[7:4]), .V(V));
endmodule
