// Digital circuit Decrementator (1 bit).dig as structural Verilog
module Decrementator__1_bit (
  input  A,
  input  B,
  input  C,
  output S,
  output V
);

  wire half_subtractor_1_s, half_subtractor_1_v, half_subtractor_2_v;

  Half_Subtractor half_subtractor_1 (.A(A), .B(B), .S(half_subtractor_1_s), .V(half_subtractor_1_v));
  Half_Subtractor half_subtractor_2 (.A(half_subtractor_1_s), .B(C), .S(S), .V(half_subtractor_2_v));
  or or_1 (V, half_subtractor_1_v, half_subtractor_2_v);
endmodule
