// Digital circuit Negativizer (2 bit).dig as structural Verilog
module Negativizer__2_bit (
  input  [1:0] In,
  output [1:0] Out
);

  xor xor_1 (Out[1], In[0], In[1]);

  assign Out[0] = In[0];
endmodule
