// Digital circuit Negativizer (4 bit).dig as structural Verilog
module Negativizer__4_bit (
  input  [3:0] In,
  output [3:0] Out
);

  wire half_negativizer_1_act, half_negativizer_2_act;

  Half_Negativizer half_negativizer_1 (
    .Act1(In[0]), .Act2(1'b0), .Curr(In[1]), .Val(Out[1]), .Act(half_negativizer_1_act));
  Half_Negativizer half_negativizer_2 (
    .Act1(half_negativizer_1_act), .Act2(In[1]), .Curr(In[2]), .Val(Out[2]), .Act(half_negativizer_2_act));
  Half_Negativizer half_negativizer_3 (
    .Act1(half_negativizer_2_act), .Act2(In[2]), .Curr(In[3]), .Val(Out[3]));  // open: Act

  assign Out[0] = In[0];
endmodule
