// Digital circuit Negativizer (8 bit).dig as structural Verilog
module Negativizer__8_bit (
  input  [7:0] In,
  output [7:0] Out
);

  wire half_negativizer_1_act, half_negativizer_2_act, half_negativizer_3_act, half_negativizer_4_act,
       half_negativizer_5_act, half_negativizer_6_act;

  Half_Negativizer half_negativizer_1 (
    .Act1(In[0]), .Act2(1'b0), .Curr(In[1]), .Val(Out[1]), .Act(half_negativizer_1_act));
  Half_Negativizer half_negativizer_2 (
    .Act1(half_negativizer_1_act), .Act2(In[1]), .Curr(In[2]), .Val(Out[2]), .Act(half_negativizer_2_act));
  Half_Negativizer half_negativizer_3 (
    .Act1(half_negativizer_2_act), .Act2(In[2]), .Curr(In[3]), .Val(Out[3]), .Act(half_negativizer_3_act));
  Half_Negativizer half_negativizer_4 (
    .Act1(half_negativizer_3_act), .Act2(In[3]), .Curr(In[4]), .Val(Out[4]), .Act(half_negativizer_4_act));
  Half_Negativizer half_negativizer_5 (
    .Act1(half_negativizer_4_act), .Act2(In[4]), .Curr(In[5]), .Val(Out[5]), .Act(half_negativizer_5_act));
  Half_Negativizer half_negativizer_6 (
    .Act1(half_negativizer_5_act), .Act2(In[5]), .Curr(In[6]), .Val(Out[6]), .Act(half_negativizer_6_act));
  Half_Negativizer half_negativizer_7 (
    .Act1(half_negativizer_6_act), .Act2(In[6]), .Curr(In[7]), .Val(Out[7]));  // open: Act

  assign Out[0] = In[0];
endmodule
