// Digital circuit Half Negativizer.dig as structural Verilog
module Half_Negativizer (
  input  Act1,
  input  Act2,
  input  Curr,
  output Val,
  output Act
);

  or or_1 (Act, Act1, Act2);
  xor xor_1 (Val, Act, Curr);
endmodule
