// Digital circuit Multiplexer (1 bit, 16x1).dig as structural Verilog
module Multiplexer__1_bit__16x1 (
  input  s0,
  input  s1,
  input  s2,
  input  s3,
  input  s4,
  input  s5,
  input  s6,
  input  s7,
  input  s8,
  input  s9,
  input  s10,
  input  s11,
  input  s12,
  input  s13,
  input  s14,
  input  s15,
  input  [3:0] sel,
  output S
);

  wire and_1_out, and_2_out, multiplexer__1_bit__8x1_1_s, multiplexer__1_bit__8x1_2_s;

  Multiplexer__1_bit__8x1 multiplexer__1_bit__8x1_1 (
    .s0(s0), .s1(s1), .s2(s2), .s3(s3), .s4(s4), .s5(s5), .s6(s6), .s7(s7), .sel(sel[2:0]),
    .S(multiplexer__1_bit__8x1_1_s));
  Multiplexer__1_bit__8x1 multiplexer__1_bit__8x1_2 (
    .s0(s8), .s1(s9), .s2(s10), .s3(s11), .s4(s12), .s5(s13), .s6(s14), .s7(s15), .sel(sel[2:0]),
    .S(multiplexer__1_bit__8x1_2_s));
  and and_1 (and_1_out, multiplexer__1_bit__8x1_1_s, ~sel[3]);  // And
  and and_2 (and_2_out, multiplexer__1_bit__8x1_2_s, sel[3]);
  or or_1 (S, and_1_out, and_2_out);
endmodule
