// Digital circuit Multiplexer (1 bit, 2x1).dig as structural Verilog
module Multiplexer__1_bit__2x1 (
  input  [1:0] sig,
  input  sel,
  output Z
);

  wire and_1_out, and_2_out;

  and and_1 (and_1_out, sig[0], ~sel);  // And
  and and_2 (and_2_out, sig[1], sel);
  or or_1 (Z, and_1_out, and_2_out);
endmodule
