// Digital circuit Multiplexer (1 bit, 32x1).dig as structural Verilog
module Multiplexer__1_bit__32x1 (
  input  s0,
  input  s1,
  input  s2,
  input  s3,
  input  s4,
  input  s5,
  input  s6,
  input  s7,
  input  s8,
  input  s9,
  input  s10,
  input  s11,
  input  s12,
  input  s13,
  input  s14,
  input  s15,
  input  s16,
  input  s17,
  input  s18,
  input  s19,
  input  s20,
  input  s21,
  input  s22,
  input  s23,
  input  s24,
  input  s25,
  input  s26,
  input  s27,
  input  s28,
  input  s29,
  input  s30,
  input  s31,
  input  [4:0] sel,
  output S
);

  wire and_1_out, and_2_out, multiplexer__1_bit__16x1_1_s, multiplexer__1_bit__16x1_2_s;

  Multiplexer__1_bit__16x1 multiplexer__1_bit__16x1_1 (
    .s0(s0), .s1(s1), .s2(s2), .s3(s3), .s4(s4), .s5(s5), .s6(s6), .s7(s7), .s8(s8), .s9(s9), .s10(s10),
    .s11(s11), .s12(s12), .s13(s13), .s14(s14), .s15(s15), .sel(sel[3:0]), .S(multiplexer__1_bit__16x1_1_s));
  Multiplexer__1_bit__16x1 multiplexer__1_bit__16x1_2 (
    .s0(s16), .s1(s17), .s2(s18), .s3(s19), .s4(s20), .s5(s21), .s6(s22), .s7(s23), .s8(s24), .s9(s25),
    .s10(s26), .s11(s27), .s12(s28), .s13(s29), .s14(s30), .s15(s31), .sel(sel[3:0]),
    .S(multiplexer__1_bit__16x1_2_s));
  and and_1 (and_1_out, multiplexer__1_bit__16x1_1_s, ~sel[4]);  // And
  and and_2 (and_2_out, multiplexer__1_bit__16x1_2_s, sel[4]);
  or or_1 (S, and_1_out, and_2_out);
endmodule
