// Digital circuit Multiplexer (1 bit, 4x1).dig as structural Verilog
module Multiplexer__1_bit__4x1 (
  input  s0,
  input  s1,
  input  s2,
  input  s3,
  input  [1:0] sel,
  output S
);

  wire and_1_out, and_2_out, multiplexer__1_bit__2x1_1_s, multiplexer__1_bit__2x1_2_s;

  Multiplexer__1_bit__2x1 multiplexer__1_bit__2x1_1 (.s0(s0), .s1(s1), .sel(sel[0]), .S(multiplexer__1_bit__2x1_1_s));
  Multiplexer__1_bit__2x1 multiplexer__1_bit__2x1_2 (.s0(s2), .s1(s3), .sel(sel[0]), .S(multiplexer__1_bit__2x1_2_s));
  and and_1 (and_1_out, multiplexer__1_bit__2x1_1_s, ~sel[1]);  // And
  and and_2 (and_2_out, multiplexer__1_bit__2x1_2_s, sel[1]);
  or or_1 (S, and_1_out, and_2_out);
endmodule
