// Digital circuit Multiplexer (1 bit, 8x1).dig as structural Verilog
module Multiplexer__1_bit__8x1 (
  input  s0,
  input  s1,
  input  s2,
  input  s3,
  input  s4,
  input  s5,
  input  s6,
  input  s7,
  input  [2:0] sel,
  output S
);

  wire and_1_out, and_2_out, multiplexer__1_bit__4x1_1_s, multiplexer__1_bit__4x1_2_s;

  Multiplexer__1_bit__4x1 multiplexer__1_bit__4x1_1 (
    .s0(s0), .s1(s1), .s2(s2), .s3(s3), .sel(sel[1:0]), .S(multiplexer__1_bit__4x1_1_s));
  Multiplexer__1_bit__4x1 multiplexer__1_bit__4x1_2 (
    .s0(s4), .s1(s5), .s2(s6), .s3(s7), .sel(sel[1:0]), .S(multiplexer__1_bit__4x1_2_s));
  and and_1 (and_1_out, multiplexer__1_bit__4x1_1_s, ~sel[2]);  // And
  and and_2 (and_2_out, multiplexer__1_bit__4x1_2_s, sel[2]);
  or or_1 (S, and_1_out, and_2_out);
endmodule
