// Digital circuit Multiplexer (2 bit, 16x1).dig as structural Verilog
module Multiplexer__2_bit__16x1 (
  input  [31:0] sig,
  input  [3:0] sel,
  output [1:0] Z
);

  wire [1:0] and_1_out, and_2_out, multiplexer__2_bit__8x1_1_z, multiplexer__2_bit__8x1_2_z,
       repeater__1_bit__1x2_1_r, repeater__1_bit__1x2_2_r;

  Multiplexer__2_bit__8x1 multiplexer__2_bit__8x1_1 (.sig(sig[15:0]), .sel(sel[2:0]), .Z(multiplexer__2_bit__8x1_1_z));
  Multiplexer__2_bit__8x1 multiplexer__2_bit__8x1_2 (.sig(sig[31:16]), .sel(sel[2:0]), .Z(multiplexer__2_bit__8x1_2_z));
  Repeater__1_bit__1x2 repeater__1_bit__1x2_1 (.S(sel[3]), .R(repeater__1_bit__1x2_1_r));
  Repeater__1_bit__1x2 repeater__1_bit__1x2_2 (.S(sel[3]), .R(repeater__1_bit__1x2_2_r));
  assign and_1_out = multiplexer__2_bit__8x1_1_z & ~repeater__1_bit__1x2_1_r;  // And and_1, 2 bits wide
  assign and_2_out = multiplexer__2_bit__8x1_2_z & repeater__1_bit__1x2_2_r;  // And and_2, 2 bits wide
  assign Z = and_1_out | and_2_out;  // Or or_1, 2 bits wide
endmodule
