// Digital circuit Multiplexer (2 bit, 2x1).dig as structural Verilog
module Multiplexer__2_bit__2x1 (
  input  [3:0] sig,
  input  sel,
  output [1:0] Z
);

  wire [1:0] and_1_out, and_2_out, repeater__1_bit__1x2_1_r, repeater__1_bit__1x2_2_r;

  Repeater__1_bit__1x2 repeater__1_bit__1x2_1 (.S(sel), .R(repeater__1_bit__1x2_1_r));
  Repeater__1_bit__1x2 repeater__1_bit__1x2_2 (.S(sel), .R(repeater__1_bit__1x2_2_r));
  assign and_1_out = sig[1:0] & ~repeater__1_bit__1x2_1_r;  // And and_1, 2 bits wide
  assign and_2_out = sig[3:2] & repeater__1_bit__1x2_2_r;  // And and_2, 2 bits wide
  assign Z = and_1_out | and_2_out;  // Or or_1, 2 bits wide
endmodule
