// Digital circuit Multiplexer (4 bit, 16x1).dig as structural Verilog
module Multiplexer__4_bit__16x1 (
  input  [63:0] sig,
  input  [3:0] sel,
  output [3:0] Z
);

  wire [3:0] and_1_out, and_2_out, multiplexer__4_bit__8x1_1_z, multiplexer__4_bit__8x1_2_z,
       repeater__1_bit__1x4_1_r, repeater__1_bit__1x4_2_r;

  Multiplexer__4_bit__8x1 multiplexer__4_bit__8x1_1 (.sig(sig[31:0]), .sel(sel[2:0]), .Z(multiplexer__4_bit__8x1_1_z));
  Multiplexer__4_bit__8x1 multiplexer__4_bit__8x1_2 (.sig(sig[63:32]), .sel(sel[2:0]), .Z(multiplexer__4_bit__8x1_2_z));
  Repeater__1_bit__1x4 repeater__1_bit__1x4_1 (.S(sel[3]), .R(repeater__1_bit__1x4_1_r));
  Repeater__1_bit__1x4 repeater__1_bit__1x4_2 (.S(sel[3]), .R(repeater__1_bit__1x4_2_r));
  assign and_1_out = multiplexer__4_bit__8x1_1_z & ~repeater__1_bit__1x4_1_r;  // And and_1, 4 bits wide
  assign and_2_out = multiplexer__4_bit__8x1_2_z & repeater__1_bit__1x4_2_r;  // And and_2, 4 bits wide
  assign Z = and_1_out | and_2_out;  // Or or_1, 4 bits wide
endmodule
