// Digital circuit Multiplexer (4 bit, 2x1).dig as structural Verilog
module Multiplexer__4_bit__2x1 (
  input  [7:0] sig,
  input  sel,
  output [3:0] Z
);

  wire [3:0] and_1_out, and_2_out, repeater__1_bit__1x4_1_r, repeater__1_bit__1x4_2_r;

  Repeater__1_bit__1x4 repeater__1_bit__1x4_1 (.S(sel), .R(repeater__1_bit__1x4_1_r));
  Repeater__1_bit__1x4 repeater__1_bit__1x4_2 (.S(sel), .R(repeater__1_bit__1x4_2_r));
  assign and_1_out = sig[3:0] & ~repeater__1_bit__1x4_1_r;  // And and_1, 4 bits wide
  assign and_2_out = sig[7:4] & repeater__1_bit__1x4_2_r;  // And and_2, 4 bits wide
  assign Z = and_1_out | and_2_out;  // Or or_1, 4 bits wide
endmodule
