// Digital circuit Multiplexer (4 bit, 32x1).dig as structural Verilog
module Multiplexer__4_bit__32x1 (
  input  [63:0] sig,
  input  [4:0] sel,
  output [3:0] Z
);

  wire [3:0] and_1_out, and_2_out, multiplexer__4_bit__16x1_1_z, multiplexer__4_bit__16x1_2_z,
       repeater__1_bit__1x4_1_r, repeater__1_bit__1x4_2_r;
  wire [63:0] undriven, undriven_2;

  Multiplexer__4_bit__16x1 multiplexer__4_bit__16x1_1 (
    .sig(undriven_2), .sel(sel[3:0]), .Z(multiplexer__4_bit__16x1_1_z));
  Multiplexer__4_bit__16x1 multiplexer__4_bit__16x1_2 (
    .sig(undriven), .sel(sel[3:0]), .Z(multiplexer__4_bit__16x1_2_z));
  Repeater__1_bit__1x4 repeater__1_bit__1x4_1 (.S(sel[4]), .R(repeater__1_bit__1x4_1_r));
  Repeater__1_bit__1x4 repeater__1_bit__1x4_2 (.S(sel[4]), .R(repeater__1_bit__1x4_2_r));
  assign and_1_out = multiplexer__4_bit__16x1_1_z & ~repeater__1_bit__1x4_1_r;  // And and_1, 4 bits wide
  assign and_2_out = multiplexer__4_bit__16x1_2_z & repeater__1_bit__1x4_2_r;  // And and_2, 4 bits wide
  assign Z = and_1_out | and_2_out;  // Or or_1, 4 bits wide
endmodule
