// Digital circuit Repeater (1 bit, 1x16).dig as structural Verilog
module Repeater__1_bit__1x16 (
  input  S,
  output [15:0] R
);

  Repeater__1_bit__1x8 repeater__1_bit__1x8_1 (.S(S), .R(R[7:0]));
  Repeater__1_bit__1x8 repeater__1_bit__1x8_2 (.S(S), .R(R[15:8]));
endmodule
