// Digital circuit Repeater (1 bit, 1x32).dig as structural Verilog
module Repeater__1_bit__1x32 (
  input  S,
  output [31:0] R
);

  Repeater__1_bit__1x16 repeater__1_bit__1x16_1 (.S(S), .R(R[15:0]));
  Repeater__1_bit__1x16 repeater__1_bit__1x16_2 (.S(S), .R(R[31:16]));
endmodule
