// Digital circuit Repeater (1 bit, 1x4).dig as structural Verilog
module Repeater__1_bit__1x4 (
  input  S,
  output [3:0] R
);

  Repeater__1_bit__1x2 repeater__1_bit__1x2_1 (.S(S), .R(R[1:0]));
  Repeater__1_bit__1x2 repeater__1_bit__1x2_2 (.S(S), .R(R[3:2]));
endmodule
