// Digital circuit Repeater (1 bit, 1x8).dig as structural Verilog
module Repeater__1_bit__1x8 (
  input  S,
  output [7:0] R
);

  Repeater__1_bit__1x4 repeater__1_bit__1x4_1 (.S(S), .R(R[3:0]));
  Repeater__1_bit__1x4 repeater__1_bit__1x4_2 (.S(S), .R(R[7:4]));
endmodule
