// Digital circuit Adder & Subtractor (4 bit).dig as structural Verilog
module Adder___Subtractor__4_bit (
  input  [3:0] A,
  input  [3:0] B,
  input  S_2,
  output [3:0] S,
  output V
);

  wire adder__1_bit_2_v, adder__1_bit_3_v, adder__1_bit_4_v, xor_1_out, xor_2_out, xor_3_out, xor_4_out;

  xor xor_1 (xor_1_out, B[3], S_2);
  Adder__1_bit adder__1_bit_1 (.A(A[3]), .B(xor_1_out), .C(adder__1_bit_2_v), .S(S[3]), .V(V));
  xor xor_2 (xor_2_out, B[2], S_2);
  xor xor_3 (xor_3_out, B[1], S_2);
  Adder__1_bit adder__1_bit_2 (.A(A[2]), .B(xor_2_out), .C(adder__1_bit_3_v), .S(S[2]), .V(adder__1_bit_2_v));
  xor xor_4 (xor_4_out, B[0], S_2);
  Adder__1_bit adder__1_bit_3 (.A(A[1]), .B(xor_3_out), .C(adder__1_bit_4_v), .S(S[1]), .V(adder__1_bit_3_v));
  Adder__1_bit adder__1_bit_4 (.A(A[0]), .B(xor_4_out), .C(S_2), .S(S[0]), .V(adder__1_bit_4_v));
endmodule
