// Digital circuit Adder & Subtractor (4 bit).dig as structural Verilog
module Adder___Subtractor__4_bit (
  input  [3:0] A,
  input  [3:0] B,
  input  S_2,
  output [3:0] S,
  output V
);

  wire full_adder__1_bit_1_p3, full_adder__1_bit_2_p3, full_adder__1_bit_3_p3, xor_1_out, xor_2_out,
       xor_3_out, xor_4_out;

  xor xor_1 (xor_1_out, B[3], S_2);
  // Full_Adder__1_bit full_adder__1_bit_1: pin names not known; wires that end beside it: A[3], xor_1_out, full_adder__1_bit_1_p3, S[3], V
  xor xor_2 (xor_2_out, B[2], S_2);
  xor xor_3 (xor_3_out, B[1], S_2);
  // Full_Adder__1_bit full_adder__1_bit_2: pin names not known; wires that end beside it: A[2], xor_2_out, full_adder__1_bit_2_p3, S[2], full_adder__1_bit_1_p3
  xor xor_4 (xor_4_out, B[0], S_2);
  // Full_Adder__1_bit full_adder__1_bit_3: pin names not known; wires that end beside it: A[1], xor_3_out, full_adder__1_bit_3_p3, S[1], full_adder__1_bit_2_p3
  // Full_Adder__1_bit full_adder__1_bit_4: pin names not known; wires that end beside it: A[0], xor_4_out, S_2, S[0], full_adder__1_bit_3_p3
endmodule
