// Digital circuit Adder (4 bit).dig as structural Verilog
module Adder__4_bit (
  input  [3:0] A,
  input  [3:0] B,
  input  C,
  output [3:0] S,
  output V
);

  wire adder__1_bit_2_v, adder__1_bit_3_v, adder__1_bit_4_v;

  Adder__1_bit adder__1_bit_1 (.A(A[3]), .B(B[3]), .C(adder__1_bit_2_v), .S(S[3]), .V(V));
  Adder__1_bit adder__1_bit_2 (.A(A[2]), .B(B[2]), .C(adder__1_bit_3_v), .S(S[2]), .V(adder__1_bit_2_v));
  Adder__1_bit adder__1_bit_3 (.A(A[1]), .B(B[1]), .C(adder__1_bit_4_v), .S(S[1]), .V(adder__1_bit_3_v));
  Adder__1_bit adder__1_bit_4 (.A(A[0]), .B(B[0]), .C(C), .S(S[0]), .V(adder__1_bit_4_v));
endmodule
