// Digital circuit Adder (4 bit).dig as structural Verilog
module Adder__4_bit (
  input  [3:0] A,
  input  [3:0] B,
  input  S_2,
  output [3:0] S,
  output V
);

  wire full_adder_2_v, full_adder_3_v, full_adder_4_v, xor_1_out, xor_2_out, xor_3_out, xor_4_out;

  xor xor_1 (xor_1_out, B[3], S_2);
  Full_Adder full_adder_1 (.A(A[3]), .B(xor_1_out), .C(full_adder_2_v), .S(S[3]), .V(V));
  xor xor_2 (xor_2_out, B[2], S_2);
  xor xor_3 (xor_3_out, B[1], S_2);
  Full_Adder full_adder_2 (.A(A[2]), .B(xor_2_out), .C(full_adder_3_v), .S(S[2]), .V(full_adder_2_v));
  xor xor_4 (xor_4_out, B[0], S_2);
  Full_Adder full_adder_3 (.A(A[1]), .B(xor_3_out), .C(full_adder_4_v), .S(S[1]), .V(full_adder_3_v));
  Full_Adder full_adder_4 (.A(A[0]), .B(xor_4_out), .C(S_2), .S(S[0]), .V(full_adder_4_v));
endmodule
