// Digital circuit Multiplexer (2 bit).dig as structural Verilog
module Multiplexer__2_bit (
  input  A,
  input  B,
  input  C,
  input  D,
  input  [1:0] sel,
  output Z
);

  wire and_1_out, and_2_out, multiplexer__1_bit_1_z, multiplexer__1_bit_2_z;

  Multiplexer__1_bit multiplexer__1_bit_1 (.A(A), .B(B), .sel(sel[0]), .Z(multiplexer__1_bit_1_z));
  Multiplexer__1_bit multiplexer__1_bit_2 (.A(C), .B(D), .sel(sel[0]), .Z(multiplexer__1_bit_2_z));
  and and_1 (and_1_out, multiplexer__1_bit_1_z, ~sel[1]);  // And
  and and_2 (and_2_out, multiplexer__1_bit_2_z, sel[1]);
  or or_1 (Z, and_1_out, and_2_out);
endmodule
