// Digital circuit Multiplexer (3 bit).dig as structural Verilog
module Multiplexer__3_bit (
  input  B,
  input  C,
  input  F,
  input  G,
  input  [2:0] sel,
  input  A,
  input  D,
  input  E,
  input  H,
  output Z
);

  wire and_1_out, and_2_out, multiplexer__2_bit_1_z, multiplexer__2_bit_2_z;

  Multiplexer__2_bit multiplexer__2_bit_1 (.A(A), .B(B), .C(C), .D(D), .sel(sel[1:0]), .Z(multiplexer__2_bit_1_z));
  Multiplexer__2_bit multiplexer__2_bit_2 (.A(E), .B(F), .C(G), .D(H), .sel(sel[1:0]), .Z(multiplexer__2_bit_2_z));
  and and_1 (and_1_out, multiplexer__2_bit_1_z, ~sel[2]);  // And
  and and_2 (and_2_out, multiplexer__2_bit_2_z, sel[2]);
  or or_1 (Z, and_1_out, and_2_out);
endmodule
