// Digital circuit SR-LATCH (NAND).dig as structural Verilog
module SR_LATCH__NAND (
  input  R,
  input  S,
  output Q,
  output nQ
);

  wire not_1_out, not_2_out;

  nand nand_1 (Q, not_1_out, nQ);
  not not_1 (not_1_out, R);
  nand nand_2 (nQ, Q, not_2_out);
  not not_2 (not_2_out, S);
endmodule
