// Digital circuit and.dig as structural Verilog
module \and  (
  input  in_1,
  input  in_2,
  output out_3
);

  wire nand_1_out;

  nand nand_1 (nand_1_out, in_1, in_2);
  nand nand_2 (out_3, nand_1_out, 1'b1);
endmodule
